# Fritzing sketch GassOff (saved by Fritzing 0.9.4)
breadboards: 2

parts:
  YwRobot_Power_Supply1 = YwRobot Breadboard Power Supply [part_number=545043]
  M1 = DOIT Esp32 DevKit v1 (30 pins long, 11 pins width) [part_number=ESP32S-PIN30]
  Componente1 = Jtron 1 Channel Optoisolated Relay Module [package=relay]
  YF-S201_Flow_Meter1 = YF-S201 Water Flow Meter
  SW-1 = Vibration sensor module
  LED1 = smd LED [color="Red (633nm)" package="0805 [SMD]"]  # not connected
  R1 = Resistor [tolerance=±5% resistance=220 package="0805 [SMD]"]
  VALVE1 = Plastic Solenoid Valve

nets:
  VCC: YwRobot_Power_Supply1.VCC#5, YwRobot_Power_Supply1.VCC#6, YF-S201_Flow_Meter1.VCC, SW-1.vcc
  N1: YwRobot_Power_Supply1.VCC#9, YwRobot_Power_Supply1.VCC#10, M1.VIN
  N2: YwRobot_Power_Supply1.GND#11, YwRobot_Power_Supply1.GND#12, YF-S201_Flow_Meter1.SIG, SW-1.Digital_output
  GND: YwRobot_Power_Supply1.GND#13, YwRobot_Power_Supply1.GND#14, M1.GND, Componente1.GND, R1.Pin_1
  N3: M1.D15, Componente1.IN1
  N4: M1.D2, SW-1.Ground
  N5: M1.D5, YF-S201_Flow_Meter1.GND
  N6: Componente1.NO, VALVE1.no_name_yet#2

notes:
  Conexión Eléctrica

custom parts:
  YwRobot Breadboard Power Supply: The YwRobot Breadboard Power Supply (MB-V2) has two power rails; they can be 5V or 3V3. Power to the module can be provided through the female USB socket or through the A10 (female) 2.1mm power jack.
  DOIT Esp32 DevKit v1 (30 pins long, 11 pins width): The DOIT Esp32 DevKit v1 is one of the development board created by DOIT to evaluate the ESP-WROOM-32 module. It is based on the ESP32 microcontroller that boasts Wifi, Bluetooth, Ethernet and Low Power support all in a single chip. (vanepp) made breadboard work, adjusted pin numbering and labels and reduced size of schematic and cleaned up pcb. This chip is 30pins long (2 x15) and 11 pins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
  YF-S201 Water Flow Meter: The YF-S201 Flow Meter. The input voltage is 5V to 24V (DC).
  Vibration sensor module: Single-roller type full induction trigger switch. When no vibration or tilt, the product is ON conduction state, and in the steady state, when a vibration or tilt, the switch will be rendered instantly disconnect the conductive resistance increases, generating a current pulse signal, thereby triggering circuit. The default state of the swith is close Digital output Supply voltage:3.3V-5V On-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

// code stored in the sketch: 0_Print_IP_Address.ino
#include "ESP8266WiFi.h"

// WiFi parameters to be configured
const char* ssid = "Mi_WiFi";
const char* password = "MY_Password";

void setup(void)
{ 
  Serial.begin(9600);
  // Connect to WiFi
  WiFi.begin(ssid, password);

  // while wifi not connected yet, print '.'
  // then after it connected, get out of the loop
  while (WiFi.status() != WL_CONNECTED) {
     delay(500);
     Serial.print(".");
  }
  //print a new line, then print WiFi connected and the IP address
  Serial.println("");
  Serial.println("WiFi connected");
  // Print the IP address
  Serial.println(WiFi.localIP());

}
void loop() {
  // Nothing
}
